# Fritzing sketch PushButtons_inv (saved by Fritzing 0.9.4)
breadboards: 1

parts:
  Raspberry_Pi_1 = Raspberry Pi 3 [part_number=RPI-3-V1.2]
  S1 = Momentary Switch [package=ksa_sealed_tac_switch]
  S2 = Momentary Switch [package=ksa_sealed_tac_switch]

nets:
  N1: Raspberry_Pi_1.3v3, S1.1, S2.1
  N2: Raspberry_Pi_1.GPIO21, S2.3
  N3: Raspberry_Pi_1.GPIO20, S1.3

notes:
  Connected on GPIO-20
  Connected on GPIO-21
  UNUSUAL BUTTONS WIRING !!
