# Fritzing sketch RPiZeroBME280 (saved by Fritzing 0.9.4)
breadboards: 1

parts:
  MCU1 = Raspberry Pi Zero
  Part1 = BME280 Breakout

nets:
  N1: MCU1.pin_1, Part1.3.3V
  N2: MCU1.pin_3, Part1.SDI/SDA
  N3: MCU1.pin_5, Part1.SCK/SCL
  N4: MCU1.pin_6, Part1.GND
